// Logisim project lab8.circ as structural Verilog: 2 circuits, main circuit main
module main (
  input  [3:0] Y,
  input  [3:0] X,
  input  Cin,
  output [4:0] S
);

  wire full_adder_1_c, full_adder_2_c, full_adder_3_c;

  Full_Adder full_adder_1 (.X(X[0]), .Y(Y[0]), .Z(Cin), .S(S[0]), .C(full_adder_1_c));
  Full_Adder full_adder_2 (.X(X[1]), .Y(Y[1]), .Z(full_adder_1_c), .S(S[1]), .C(full_adder_2_c));
  Full_Adder full_adder_3 (.X(X[2]), .Y(Y[2]), .Z(full_adder_2_c), .S(S[2]), .C(full_adder_3_c));
  Full_Adder full_adder_4 (.X(X[3]), .Y(Y[3]), .Z(full_adder_3_c), .S(S[3]), .C(S[4]));
endmodule

module Full_Adder (
  input  X,
  input  Y,
  input  Z,
  output S,
  output C
);

  wire and_1_out, and_2_out, xor_1_out;

  xor xor_1 (xor_1_out, X, Y);
  and and_1 (and_1_out, X, Y);
  xor xor_2 (S, xor_1_out, Z);
  and and_2 (and_2_out, xor_1_out, Z);
  or or_1 (C, and_2_out, and_1_out);
endmodule
